// Logisim project aphelion2.circ as structural Verilog: 1 circuit, main circuit main
module main (
  input  [3:0] opcode,
  input  [7:0] arg1,
  input  [7:0] arg2,
  input  [7:0] arg3
);

  wire clock_1_out;

  Clock clock_1 (.out(clock_1_out));
endmodule
